// Logisim project S2-T19.circ as structural Verilog: 5 circuits, main circuit main
// Binary Sequence Generator
module main (
  input  Pay_5000,
  input  Pay_500
);

  wire and_1_out, and_2_out, and_3_out, BCD_to_7_Segment_Decoder_2_a, BCD_to_7_Segment_Decoder_2_b,
       BCD_to_7_Segment_Decoder_2_c, BCD_to_7_Segment_Decoder_2_d, BCD_to_7_Segment_Decoder_2_e,
       BCD_to_7_Segment_Decoder_2_f, BCD_to_7_Segment_Decoder_2_g, BCD_to_7_Segment_Decoder_a,
       BCD_to_7_Segment_Decoder_b, BCD_to_7_Segment_Decoder_c, BCD_to_7_Segment_Decoder_d,
       BCD_to_7_Segment_Decoder_e, BCD_to_7_Segment_Decoder_f, BCD_to_7_Segment_Decoder_g,
       Binary_Sequence_Generator_2_out_3, Binary_Sequence_Generator_out_3, button_1_out, button_2_out,
       button_3_out, clock_1_out, clock_2_out, clock_3_out, counter_1_carry, Decoder_a, Decoder_b, Decoder_c,
       Decoder_d, Decoder_e, Decoder_f, Decoder_g, or_1_out, or_2_out, Random_Number_Generator_2_out_4,
       Random_Number_Generator_2_out_5, Random_Number_Generator_2_out_6, Random_Number_Generator_3_out_4,
       Random_Number_Generator_3_out_5, Random_Number_Generator_3_out_6, Random_Number_Generator_out_4,
       Random_Number_Generator_out_5, Random_Number_Generator_out_6;

  Button button_1 (.out(button_1_out));
  Button button_2 (.out(button_2_out));
  Button button_3 (.out(button_3_out));
  Clock #(.highDuration(3)) clock_1 (.out(clock_1_out));
  Clock #(.highDuration(7)) clock_2 (.out(clock_2_out));
  Clock #(.highDuration(5), .lowDuration(2)) clock_3 (.out(clock_3_out));
  or or_1 (or_1_out, button_1_out, button_2_out);
  binary_sequence_generator_2 Binary_Sequence_Generator (
    .in_1(Pay_500), .in_2(button_3_out), .out_3(Binary_Sequence_Generator_out_3));
  binary_sequence_generator_1 Binary_Sequence_Generator_2 (
    .in_1(Pay_5000), .in_2(button_3_out), .out_3(Binary_Sequence_Generator_2_out_3));
  Counter #(.width(4), .max('hf)) counter_1 (
    .carry(counter_1_carry), .clk(button_3_out), .clr(or_1_out));  // open: load, D, count, Q
  or or_2 (or_2_out, counter_1_carry, Binary_Sequence_Generator_2_out_3, Binary_Sequence_Generator_out_3, button_2_out);
  and and_1 (and_1_out, clock_1_out, button_3_out);
  and and_2 (and_2_out, clock_2_out, button_3_out);
  and and_3 (and_3_out, clock_3_out, button_3_out);
  random_number_generator Random_Number_Generator (
    .Clock(and_1_out), .in_2(or_2_out), .Preset(or_2_out), .out_4(Random_Number_Generator_out_4),
    .out_5(Random_Number_Generator_out_5), .out_6(Random_Number_Generator_out_6));
  random_number_generator Random_Number_Generator_2 (
    .Clock(and_2_out), .in_2(or_2_out), .Preset(or_2_out), .out_4(Random_Number_Generator_2_out_4),
    .out_5(Random_Number_Generator_2_out_5), .out_6(Random_Number_Generator_2_out_6));
  random_number_generator Random_Number_Generator_3 (
    .Clock(and_3_out), .in_2(or_2_out), .Preset(or_2_out), .out_4(Random_Number_Generator_3_out_4),
    .out_5(Random_Number_Generator_3_out_5), .out_6(Random_Number_Generator_3_out_6));
  bcd_to_7_segment_decoder BCD_to_7_Segment_Decoder (
    .x(Random_Number_Generator_out_4), .y(Random_Number_Generator_out_5), .z(Random_Number_Generator_out_6),
    .a(BCD_to_7_Segment_Decoder_a), .b(BCD_to_7_Segment_Decoder_b), .c(BCD_to_7_Segment_Decoder_c),
    .d(BCD_to_7_Segment_Decoder_d), .e(BCD_to_7_Segment_Decoder_e), .f(BCD_to_7_Segment_Decoder_f),
    .g(BCD_to_7_Segment_Decoder_g));
  bcd_to_7_segment_decoder BCD_to_7_Segment_Decoder_2 (
    .x(Random_Number_Generator_3_out_4), .y(Random_Number_Generator_3_out_5),
    .z(Random_Number_Generator_3_out_6), .a(BCD_to_7_Segment_Decoder_2_a), .b(BCD_to_7_Segment_Decoder_2_b),
    .c(BCD_to_7_Segment_Decoder_2_c), .d(BCD_to_7_Segment_Decoder_2_d), .e(BCD_to_7_Segment_Decoder_2_e),
    .f(BCD_to_7_Segment_Decoder_2_f), .g(BCD_to_7_Segment_Decoder_2_g));
  bcd_to_7_segment_decoder Decoder (
    .x(Random_Number_Generator_2_out_4), .y(Random_Number_Generator_2_out_5),
    .z(Random_Number_Generator_2_out_6), .a(Decoder_a), .b(Decoder_b), .c(Decoder_c), .d(Decoder_d),
    .e(Decoder_e), .f(Decoder_f), .g(Decoder_g));
  _7_Segment_Display u_7_segment_display_1 (
    .g(BCD_to_7_Segment_Decoder_g), .f(BCD_to_7_Segment_Decoder_f), .a(BCD_to_7_Segment_Decoder_a),
    .b(BCD_to_7_Segment_Decoder_b), .e(BCD_to_7_Segment_Decoder_e), .d(BCD_to_7_Segment_Decoder_d),
    .c(BCD_to_7_Segment_Decoder_c));  // open: dp
  _7_Segment_Display u_7_segment_display_2 (
    .g(Decoder_g), .f(Decoder_f), .a(Decoder_a), .b(Decoder_b), .e(Decoder_e), .d(Decoder_d), .c(Decoder_c));  // open: dp
  _7_Segment_Display u_7_segment_display_3 (
    .g(BCD_to_7_Segment_Decoder_2_g), .f(BCD_to_7_Segment_Decoder_2_f), .a(BCD_to_7_Segment_Decoder_2_a),
    .b(BCD_to_7_Segment_Decoder_2_b), .e(BCD_to_7_Segment_Decoder_2_e), .d(BCD_to_7_Segment_Decoder_2_d),
    .c(BCD_to_7_Segment_Decoder_2_c));  // open: dp

  // Notes on the sheet:
  //   Clock 3
  //   Clock 2
  //   Clock 1
  //   END
  //   START
  //   PLAY
  //   4 Bit Counter
  //   CASINO SLOT MACHINE
  //   Overall Circuit
  //   Display 1
  //   Display 2
  //   Display 3
  //   5. Click on END to end the game
  //   Instructions
  //   1.Go to Simulate and make sure that 'Ticks Enabled' is ON
  //   2. Click on the "START" Button to reset the circuit and start the game
  //   4. Click on Pay 500 or Pay 5000 to increase the chances of winning
  //   Aman Kumar Singh 231CS206
  //   3. Push and hold the "PLAY" Button to start the machine and release it to get your result 
  //   Team ID: S2-T19
  //   Mohnish Hemanth Kumar 231CS235
  //   Rudransh Kumar Ankodia 231CS249
endmodule

module binary_sequence_generator_1 (
  input  in_1,
  input  in_2,
  output out_3
);

  wire and_1_out, and_2_out, and_3_out, d_ff_1_q, d_ff_2_q, d_ff_3_q, d_ff_4_q, not_1_out, not_2_out,
       not_3_out, not_4_out, or_1_out;

  or or_1 (or_1_out, and_2_out, and_3_out);
  and and_1 (and_1_out, in_1, in_2);
  and and_2 (and_2_out, not_4_out, not_3_out);
  and and_3 (and_3_out, not_1_out, not_2_out);
  D_Flip_Flop d_ff_1 (.clk(and_1_out), .D(or_1_out), .Q(d_ff_1_q));  // open: Qn, preset, en, reset
  not not_1 (not_1_out, d_ff_2_q);
  not not_2 (not_2_out, d_ff_1_q);
  D_Flip_Flop d_ff_2 (.clk(and_1_out), .D(d_ff_1_q), .Q(d_ff_2_q));  // open: Qn, preset, en, reset
  and and_4 (out_3, or_1_out, and_1_out);
  not not_3 (not_3_out, d_ff_3_q);
  D_Flip_Flop d_ff_3 (.clk(and_1_out), .D(d_ff_2_q), .Q(d_ff_3_q));  // open: Qn, preset, en, reset
  not not_4 (not_4_out, d_ff_4_q);
  D_Flip_Flop d_ff_4 (.clk(and_1_out), .D(d_ff_3_q), .Q(d_ff_4_q));  // open: Qn, preset, en, reset

  // Notes on the sheet:
  //   Binary Sequence Generator 1
  //   Generates the sequence '01001'
endmodule

module bcd_to_7_segment_decoder (
  input  x,
  input  y,
  input  z,
  output a,
  output b,
  output c,
  output d,
  output e,
  output f,
  output g
);

  wire and_1_out, and_2_out, and_3_out, and_4_out, and_5_out, and_6_out, and_7_out, and_8_out, and_9_out,
       and_10_out, and_11_out, and_12_out, and_13_out, and_14_out, and_15_out, and_16_out, and_17_out,
       not_1_out, not_2_out, not_3_out, or_1_out, or_2_out, or_3_out, or_6_out, or_7_out, or_10_out,
       or_11_out;

  not not_1 (not_1_out, x);
  not not_2 (not_2_out, z);
  not not_3 (not_3_out, y);
  and and_1 (and_1_out, not_1_out, not_2_out);
  and and_2 (and_2_out, not_3_out, not_2_out);
  or or_1 (or_1_out, not_3_out, z);
  and and_3 (and_3_out, x, not_3_out);
  and and_4 (and_4_out, not_1_out, not_2_out);
  and and_5 (and_5_out, y, not_2_out);
  and and_6 (and_6_out, not_3_out, not_2_out);
  and and_7 (and_7_out, x, not_3_out);
  and and_8 (and_8_out, not_1_out, y);
  and and_9 (and_9_out, x, not_3_out);
  or or_2 (or_2_out, and_1_out, y);
  and and_10 (and_10_out, x, z);
  or or_3 (or_3_out, not_1_out, and_2_out);
  and and_11 (and_11_out, y, z);
  or or_4 (c, or_1_out, x);
  and and_12 (and_12_out, not_1_out, not_2_out);
  and and_13 (and_13_out, not_1_out, y);
  and and_14 (and_14_out, y, not_2_out);
  and and_15 (and_15_out, and_3_out, z);
  or or_5 (e, and_4_out, and_5_out);
  or or_6 (or_6_out, and_6_out, and_7_out);
  and and_16 (and_16_out, x, not_2_out);
  or or_7 (or_7_out, and_8_out, and_9_out);
  and and_17 (and_17_out, x, not_2_out);
  or or_8 (a, or_2_out, and_10_out);
  or or_9 (b, or_3_out, and_11_out);
  or or_10 (or_10_out, and_12_out, and_13_out);
  or or_11 (or_11_out, and_14_out, and_15_out);
  or or_12 (f, or_6_out, and_16_out);
  or or_13 (g, or_7_out, and_17_out);
  or or_14 (d, or_10_out, or_11_out);

  // Notes on the sheet:
  //   BCD TO 7 SEGMENT DISPLAY DECODER
endmodule

module random_number_generator (
  input  Clock,
  input  in_2,
  input  Preset,
  output out_4,
  output out_5,
  output out_6
);

  wire d_ff_1_q, d_ff_2_q, d_ff_3_q, xor_1_out;

  xor xor_1 (xor_1_out, d_ff_2_q, d_ff_3_q);
  D_Flip_Flop d_ff_1 (.clk(Clock), .D(xor_1_out), .Q(d_ff_1_q), .preset(Preset));  // open: Qn, en, reset
  D_Flip_Flop d_ff_2 (.clk(Clock), .D(d_ff_1_q), .Q(d_ff_2_q));  // open: Qn, preset, en, reset
  D_Flip_Flop d_ff_3 (.clk(Clock), .D(d_ff_2_q), .Q(d_ff_3_q));  // open: Qn, preset, en, reset
  or or_1 (out_4, in_2, d_ff_1_q);
  or or_2 (out_5, d_ff_2_q, in_2);
  or or_3 (out_6, d_ff_3_q, in_2);

  // Notes on the sheet:
  //   Condition to display 7 7 7
  //   Random Number Generator using LFSR
  //   BCD output
endmodule

module binary_sequence_generator_2 (
  input  in_1,
  input  in_2,
  output out_3
);

  wire and_1_out, d_ff_1_q, d_ff_2_q, not_1_out;

  not not_1 (not_1_out, d_ff_2_q);
  and and_1 (and_1_out, in_1, in_2);
  D_Flip_Flop d_ff_1 (.clk(and_1_out), .D(not_1_out), .Q(d_ff_1_q));  // open: Qn, preset, en, reset
  D_Flip_Flop d_ff_2 (.clk(and_1_out), .D(d_ff_1_q), .Q(d_ff_2_q));  // open: Qn, preset, en, reset
  and and_2 (out_3, not_1_out, and_1_out);
  D_Flip_Flop d_ff_3 (.clk(and_1_out), .D(d_ff_2_q));  // open: Q, Qn, preset, en, reset

  // Notes on the sheet:
  //   Binary Sequence Generator 2
  //   Generates the sequence '1001'
endmodule
